# Fritzing sketch Pieper 0.8.5 (saved by Fritzing 0.9.3b)
circuit board: 8.46667cm x 5.64444cm
breadboards: 1

parts:
  Bauteil1 = Arduino Nano (Rev3.0)
  S1 = Pushbutton [package="[THT]"]
  ZS-042_RTC1 = ZS-042 RTC Module
  LCD1 = TFT 1.8 inch 160x128 w SD
  LED1 = LED - 5mm [color="Red (633nm)" package="5 mm [THT]"]
  R1 = Trimmer Potentiometer [maximum_resistance=10kΩ package=THT]
  R2 = Resistor [tolerance=±5% resistance=10k package=THT]
  R3 = Resistor [tolerance=±5% resistance=1k package=THT]
  R4 = Resistor [tolerance=±5% resistance=10k package=THT]  # not connected
  C1 = Ceramic Capacitor [capacitance=100nF package="100 mil [THT, multilayer]"]  # not connected

nets (from the pcb view):
  GND: Bauteil1.GND, S1.Pin_3, S1.Pin_4, ZS-042_RTC1.GND, LCD1.pin2, R3.Pin_0
  N1: Bauteil1.D2, S1.Pin_1, S1.Pin_2, R2.Pin_1
  N2: Bauteil1.D3, LED1.anode
  N3: Bauteil1.D4, LCD1.pin_9
  N4: Bauteil1.D8, LCD1.pin4
  N5: Bauteil1.D9, LCD1.pin_5
  N6: Bauteil1.D10, LCD1.pin3
  N7: Bauteil1.D11/MOSI, LCD1.pin_10
  N8: Bauteil1.D12/MISO, LCD1.pin_11
  5V: Bauteil1.5V, ZS-042_RTC1.VCC, LCD1.pin_1, R1.leg2, R2.Pin_0
  N9: Bauteil1.A5, ZS-042_RTC1.SCL
  N10: Bauteil1.A4, ZS-042_RTC1.SDA
  N11: Bauteil1.D13/SCK, LCD1.pin_7
  N12: LCD1.pin_8, R1.wiper
  N13: LED1.cathode, R3.Pin_1

custom parts:
  TFT 1.8 inch 160x128 w SD: This is a generic 1.8 tft spi lcd display available on ebay and others. The 1.8" display has 128x160 color pixels.
